// Logisim project Single Cycle Processor Design.circ as structural Verilog: 17 circuits, main circuit main
module main (
);

  wire ALU_zero, and_1_out, clear_out, Clock, controlunit_1_alusrc, controlunit_1_branch, controlunit_1_jump,
       controlunit_1_memread, controlunit_1_memtoreg, controlunit_1_memwrite, controlunit_1_regdst,
       controlunit_1_regwrite, not_1_out;
  wire [3:0] controlunit_1_aluop;
  wire [4:0] multiplexer_1_out, splitter_1_rd, splitter_1_rs, splitter_1_rt, splitter_1_shamt;
  wire [5:0] splitter_1_opcode;
  wire [15:0] adder_1_out, adder_2_out, ALU_result, counter_1_q, multiplexer_2_out, multiplexer_3_out,
       multiplexer_4_out, multiplexer_5_out, n16bit_register_1_read_data_1, n16bit_register_1_read_data_2,
       ram_2_data, shifter_1_out, splitter_1__0_15;
  wire [31:0] ram_1_data;

  Counter #(.width(16), .max('hffff)) counter_1 (
    .D(multiplexer_4_out), .Q(counter_1_q), .clk(Clock), .clr(clear_out));  // open: load, count, carry
  Button clear (.out(clear_out));
  Clock clock_1 (.out(Clock));
  Adder #(.width(16)) adder_1 (.a(counter_1_q), .b(16'h1), .out(adder_1_out));  // open: cin, cout
  ControlUnit controlunit_1 (
    .Opcode(splitter_1_opcode), .Jump(controlunit_1_jump), .RegDst(controlunit_1_regdst),
    .ALUSrc(controlunit_1_alusrc), .MemtoReg(controlunit_1_memtoreg), .RegWrite(controlunit_1_regwrite),
    .MemRead(controlunit_1_memread), .MemWrite(controlunit_1_memwrite), .Branch(controlunit_1_branch),
    .ALUop(controlunit_1_aluop));
  RAM #(.addrWidth(16), .dataWidth(32)) ram_1 (.addr(counter_1_q), .data(ram_1_data));  // open: sel, clk, ld, clr
  Splitter splitter_1 (
    .in_1(ram_1_data), .Opcode(splitter_1_opcode), .rs(splitter_1_rs), .rt(splitter_1_rt),
    .rd(splitter_1_rd), .shamt(splitter_1_shamt), ._0_15(splitter_1__0_15));
  Multiplexer #(.width(5)) multiplexer_1 (
    .in0(splitter_1_rt), .in1(splitter_1_rd), .out(multiplexer_1_out), .sel(controlunit_1_regdst));  // open: en
  _16bit_Register u_16bit_register_1 (
    .Read_Register_1(splitter_1_rs), .Read_Register_2(splitter_1_rt), .Write_Register(multiplexer_1_out),
    .Write_Data(multiplexer_5_out), .Read_Data_1(n16bit_register_1_read_data_1),
    .Read_Data_2(n16bit_register_1_read_data_2), .RegWrite(controlunit_1_regwrite));
  Multiplexer #(.width(16)) multiplexer_2 (
    .in0(n16bit_register_1_read_data_2), .in1(splitter_1__0_15), .out(multiplexer_2_out),
    .sel(controlunit_1_alusrc));  // open: en
  Shifter #(.width(16)) shifter_1 (.in(splitter_1__0_15), .\dist (4'b0010), .out(shifter_1_out));
  Adder #(.width(16)) adder_2 (.a(adder_1_out), .b(shifter_1_out), .out(adder_2_out));  // open: cin, cout
  and and_1 (and_1_out, controlunit_1_branch, ALU_zero);
  _16bit_ALU ALU (
    .A(n16bit_register_1_read_data_1), .B(multiplexer_2_out), .Result(ALU_result),
    .Opcode(controlunit_1_aluop), .Shamt(splitter_1_shamt), .zero(ALU_zero));  // open: Overflow
  Multiplexer #(.width(16)) multiplexer_3 (
    .in0(adder_1_out), .in1(adder_2_out), .out(multiplexer_3_out), .sel(and_1_out));  // open: en
  Multiplexer #(.width(16)) multiplexer_4 (
    .in0(multiplexer_3_out), .in1(splitter_1__0_15), .out(multiplexer_4_out), .sel(controlunit_1_jump));  // open: en
  not not_1 (not_1_out, Clock);
  RAM #(.addrWidth(16), .dataWidth(16), .bus("separate")) ram_2 (
    .addr(ALU_result), .din(n16bit_register_1_read_data_2), .data(ram_2_data), .str(controlunit_1_memwrite),
    .clk(not_1_out), .ld(controlunit_1_memread));  // open: sel, clr
  Multiplexer #(.width(16)) multiplexer_5 (
    .in0(ALU_result), .in1(ram_2_data), .out(multiplexer_5_out), .sel(controlunit_1_memtoreg));  // open: en
endmodule

module FullAdder (
  input  A,
  input  B,
  input  CarryIn,
  output S,
  output CarryOut
);

  wire and_1_out, and_2_out, xor_1_out;

  xor xor_1 (xor_1_out, A, B);
  and and_1 (and_1_out, CarryIn, xor_1_out);
  and and_2 (and_2_out, A, B);
  xor xor_2 (S, xor_1_out, CarryIn);
  or or_1 (CarryOut, and_1_out, and_2_out);
endmodule

// ADD
module _16bit_Adder (
  input  [15:0] A,
  input  [15:0] B,
  output [15:0] S,
  output CarryOut,
  output Overflow
);

  wire Adder_2_carryout, Adder_3_carryout, Adder_4_carryout, Adder_5_carryout, Adder_6_carryout,
       Adder_7_carryout, Adder_8_carryout, Adder_9_carryout, Adder_10_carryout, Adder_11_carryout,
       Adder_12_carryout, Adder_13_carryout, Adder_carryout, fulladder_1_carryout, fulladder_2_carryout,
       xor_1_out, xor_2_out;

  FullAdder fulladder_1 (.A(A[0]), .B(B[0]), .CarryIn(1'b0), .S(S[0]), .CarryOut(fulladder_1_carryout));
  FullAdder Adder (.A(A[1]), .B(B[1]), .CarryIn(fulladder_1_carryout), .S(S[1]), .CarryOut(Adder_carryout));
  FullAdder Adder_2 (.A(A[2]), .B(B[2]), .CarryIn(Adder_carryout), .S(S[2]), .CarryOut(Adder_2_carryout));
  FullAdder Adder_3 (.A(A[3]), .B(B[3]), .CarryIn(Adder_2_carryout), .S(S[3]), .CarryOut(Adder_3_carryout));
  FullAdder Adder_4 (.A(A[4]), .B(B[4]), .CarryIn(Adder_3_carryout), .S(S[4]), .CarryOut(Adder_4_carryout));
  FullAdder fulladder_2 (.A(A[5]), .B(B[5]), .CarryIn(Adder_4_carryout), .S(S[5]), .CarryOut(fulladder_2_carryout));
  FullAdder Adder_5 (.A(A[6]), .B(B[6]), .CarryIn(fulladder_2_carryout), .S(S[6]), .CarryOut(Adder_5_carryout));
  FullAdder Adder_6 (.A(A[7]), .B(B[7]), .CarryIn(Adder_5_carryout), .S(S[7]), .CarryOut(Adder_6_carryout));
  FullAdder Adder_7 (.A(A[8]), .B(B[8]), .CarryIn(Adder_6_carryout), .S(S[8]), .CarryOut(Adder_7_carryout));
  FullAdder Adder_8 (.A(A[9]), .B(B[9]), .CarryIn(Adder_7_carryout), .S(S[9]), .CarryOut(Adder_8_carryout));
  FullAdder Adder_9 (.A(A[10]), .B(B[10]), .CarryIn(Adder_8_carryout), .S(S[10]), .CarryOut(Adder_9_carryout));
  FullAdder Adder_10 (.A(A[11]), .B(B[11]), .CarryIn(Adder_9_carryout), .S(S[11]), .CarryOut(Adder_10_carryout));
  FullAdder Adder_11 (.A(A[12]), .B(B[12]), .CarryIn(Adder_10_carryout), .S(S[12]), .CarryOut(Adder_11_carryout));
  FullAdder Adder_12 (.A(A[13]), .B(B[13]), .CarryIn(Adder_11_carryout), .S(S[13]), .CarryOut(Adder_12_carryout));
  FullAdder Adder_13 (.A(A[14]), .B(B[14]), .CarryIn(Adder_12_carryout), .S(S[14]), .CarryOut(Adder_13_carryout));
  FullAdder Adder_14 (.A(A[15]), .B(B[15]), .CarryIn(Adder_13_carryout), .S(S[15]), .CarryOut(CarryOut));
  xor xor_1 (xor_1_out, A[15], B[15]);
  xor xor_2 (xor_2_out, S[15], A[15]);
  Multiplexer multiplexer_1 (.in0(xor_2_out), .in1(1'b0), .out(Overflow), .sel(xor_1_out));  // open: en
endmodule

// SUB
module _16bit_Subtractor (
  input  [15:0] A,
  input  [15:0] B,
  output [15:0] S,
  output CarryOut,
  output Overflow
);

  wire Adder_2_carryout, Adder_3_carryout, Adder_4_carryout, Adder_5_carryout, Adder_6_carryout,
       Adder_7_carryout, Adder_8_carryout, Adder_9_carryout, Adder_10_carryout, Adder_11_carryout,
       Adder_12_carryout, Adder_13_carryout, Adder_carryout, fulladder_1_carryout, fulladder_2_carryout,
       not_1_out, not_2_out, not_3_out, not_4_out, not_5_out, not_6_out, not_7_out, not_8_out, not_9_out,
       not_10_out, not_11_out, not_12_out, not_13_out, not_14_out, not_15_out, not_16_out, xor_1_out,
       xor_2_out;

  not not_1 (not_1_out, B[0]);
  not not_2 (not_2_out, B[1]);
  not not_3 (not_3_out, B[2]);
  not not_4 (not_4_out, B[3]);
  not not_5 (not_5_out, B[4]);
  not not_6 (not_6_out, B[5]);
  not not_7 (not_7_out, B[6]);
  not not_8 (not_8_out, B[7]);
  not not_9 (not_9_out, B[8]);
  not not_10 (not_10_out, B[9]);
  not not_11 (not_11_out, B[10]);
  not not_12 (not_12_out, B[11]);
  not not_13 (not_13_out, B[12]);
  not not_14 (not_14_out, B[13]);
  not not_15 (not_15_out, B[14]);
  not not_16 (not_16_out, B[15]);
  FullAdder fulladder_1 (.A(A[0]), .B(not_1_out), .CarryIn(1'b1), .S(S[0]), .CarryOut(fulladder_1_carryout));
  FullAdder Adder (.A(A[1]), .B(not_2_out), .CarryIn(fulladder_1_carryout), .S(S[1]), .CarryOut(Adder_carryout));
  FullAdder Adder_2 (.A(A[2]), .B(not_3_out), .CarryIn(Adder_carryout), .S(S[2]), .CarryOut(Adder_2_carryout));
  FullAdder Adder_3 (.A(A[3]), .B(not_4_out), .CarryIn(Adder_2_carryout), .S(S[3]), .CarryOut(Adder_3_carryout));
  FullAdder Adder_4 (.A(A[4]), .B(not_5_out), .CarryIn(Adder_3_carryout), .S(S[4]), .CarryOut(Adder_4_carryout));
  FullAdder fulladder_2 (
    .A(A[5]), .B(not_6_out), .CarryIn(Adder_4_carryout), .S(S[5]), .CarryOut(fulladder_2_carryout));
  FullAdder Adder_5 (.A(A[6]), .B(not_7_out), .CarryIn(fulladder_2_carryout), .S(S[6]), .CarryOut(Adder_5_carryout));
  FullAdder Adder_6 (.A(A[7]), .B(not_8_out), .CarryIn(Adder_5_carryout), .S(S[7]), .CarryOut(Adder_6_carryout));
  FullAdder Adder_7 (.A(A[8]), .B(not_9_out), .CarryIn(Adder_6_carryout), .S(S[8]), .CarryOut(Adder_7_carryout));
  FullAdder Adder_8 (.A(A[9]), .B(not_10_out), .CarryIn(Adder_7_carryout), .S(S[9]), .CarryOut(Adder_8_carryout));
  FullAdder Adder_9 (.A(A[10]), .B(not_11_out), .CarryIn(Adder_8_carryout), .S(S[10]), .CarryOut(Adder_9_carryout));
  FullAdder Adder_10 (.A(A[11]), .B(not_12_out), .CarryIn(Adder_9_carryout), .S(S[11]), .CarryOut(Adder_10_carryout));
  FullAdder Adder_11 (.A(A[12]), .B(not_13_out), .CarryIn(Adder_10_carryout), .S(S[12]), .CarryOut(Adder_11_carryout));
  FullAdder Adder_12 (.A(A[13]), .B(not_14_out), .CarryIn(Adder_11_carryout), .S(S[13]), .CarryOut(Adder_12_carryout));
  FullAdder Adder_13 (.A(A[14]), .B(not_15_out), .CarryIn(Adder_12_carryout), .S(S[14]), .CarryOut(Adder_13_carryout));
  FullAdder Adder_14 (.A(A[15]), .B(not_16_out), .CarryIn(Adder_13_carryout), .S(S[15]), .CarryOut(CarryOut));
  xor xor_1 (xor_1_out, A[15], not_16_out);
  xor xor_2 (xor_2_out, S[15], A[15]);
  Multiplexer multiplexer_1 (.in0(xor_2_out), .in1(1'b0), .out(Overflow), .sel(xor_1_out));  // open: en
endmodule

// ALU
module _16bit_ALU (
  input  [15:0] A,
  input  [15:0] B,
  input  [4:0] Shamt,
  input  [3:0] Opcode,
  output zero,
  output Overflow,
  output [15:0] Result
);

  wire n16bit_adder_1_overflow, n16bit_subtractor_1_overflow;
  wire [15:0] and_1_out, multiplier_2_out, n16bit_adder_1_s, n16bit_subtractor_1_s, nor_1_out, or_1_out,
       shifter_1_out;
  wire [31:0] bit_extender_1_out, bit_extender_2_out, multiplier_1_out;

  assign nor_1_out = ~(B | A);  // NOR_Gate nor_1, 16 bits wide
  assign bit_extender_1_out = {{16{1'b0}}, A};  // Bit_Extender bit_extender_1
  assign bit_extender_2_out = {{16{1'b0}}, B};  // Bit_Extender bit_extender_2
  Multiplier #(.width(32)) multiplier_1 (
    .a(bit_extender_1_out), .b(bit_extender_2_out), .out(multiplier_1_out));  // open: cin, cout
  Comparator #(.width(16)) comparator_1 (.a(A), .b(B), .lt(zero));  // open: gt, eq
  assign or_1_out = B | A;  // OR_Gate or_1, 16 bits wide
  Shifter #(.width(16)) shifter_1 (.in(A), .\dist (Shamt[3:0]), .out(shifter_1_out));
  assign and_1_out = A & B;  // AND_Gate and_1, 16 bits wide
  _16bit_Subtractor u_16bit_subtractor_1 (
    .A(A), .B(B), .S(n16bit_subtractor_1_s), .Overflow(n16bit_subtractor_1_overflow));  // open: CarryOut
  _16bit_Adder u_16bit_adder_1 (
    .A(A), .B(B), .S(n16bit_adder_1_s), .Overflow(n16bit_adder_1_overflow));  // open: CarryOut
  Multiplier #(.width(16)) multiplier_2 (.a(A), .b(B), .out(multiplier_2_out));  // open: cin, cout
  Multiplexer #(.select(4), .width(16)) multiplexer_1 (
    .in0(n16bit_adder_1_s), .in1(n16bit_subtractor_1_s), .in2(multiplier_2_out), .in3(and_1_out),
    .in4(or_1_out), .in6(shifter_1_out), .in7({{15{1'b0}}, zero}), .in8(multiplier_1_out[31:16]),
    .in9(multiplier_1_out[15:0]), .in15(nor_1_out), .out(Result), .sel(Opcode));  // open: in5, in10, in11, in12, in13, in14, en
  Multiplexer #(.select(4)) multiplexer_2 (
    .in0(n16bit_adder_1_overflow), .in1(n16bit_subtractor_1_overflow), .in2(1'b0), .in3(1'b0), .in4(1'b0),
    .in5(n16bit_adder_1_overflow), .in6(1'b0), .in7(1'b0), .in8(1'b0), .in9(1'b0), .in10(1'b0), .in11(1'b0),
    .in12(1'b0), .in13(1'b0), .in14(1'b0), .in15(1'b0), .out(Overflow), .sel(Opcode));  // open: en
endmodule

// Reg File
module _16bit_Register (
  input  [4:0] Read_Register_1,
  input  [4:0] Read_Register_2,
  input  [4:0] Write_Register,
  input  [15:0] Write_Data,
  input  RegWrite,
  output [15:0] Read_Data_1,
  output [15:0] Read_Data_2
);

  wire and_1_out, and_2_out, and_3_out, and_4_out, and_5_out, and_6_out, and_7_out, and_8_out, and_9_out,
       and_10_out, and_11_out, and_12_out, and_13_out, and_14_out, and_15_out, and_16_out, clock_out,
       decoder_1_out0, decoder_1_out1, decoder_1_out2, decoder_1_out3, decoder_1_out4, decoder_1_out5,
       decoder_1_out6, decoder_1_out7, decoder_1_out8, decoder_1_out9, decoder_1_out10, decoder_1_out11,
       decoder_1_out12, decoder_1_out13, decoder_1_out14, decoder_1_out15;
  wire [3:0] bit_extender_1_out, bit_extender_2_out, bit_extender_3_out;
  wire [15:0] register_1_q, register_2_q, register_3_q, register_4_q, register_5_q, register_6_q,
       register_7_q, register_8_q, register_9_q, register_10_q, register_11_q, register_12_q, register_13_q,
       register_14_q, register_15_q, register_16_q;

  Decoder #(.select(4)) decoder_1 (
    .out0(decoder_1_out0), .out1(decoder_1_out1), .out2(decoder_1_out2), .out3(decoder_1_out3),
    .out4(decoder_1_out4), .out5(decoder_1_out5), .out6(decoder_1_out6), .out7(decoder_1_out7),
    .out8(decoder_1_out8), .out9(decoder_1_out9), .out10(decoder_1_out10), .out11(decoder_1_out11),
    .out12(decoder_1_out12), .out13(decoder_1_out13), .out14(decoder_1_out14), .out15(decoder_1_out15),
    .sel(bit_extender_3_out));  // open: en
  Bit_Extender #(.in_width(5), .out_width(4)) bit_extender_1 (.in(Read_Register_1), .out(bit_extender_1_out));
  Bit_Extender #(.in_width(5), .out_width(4)) bit_extender_2 (.in(Read_Register_2), .out(bit_extender_2_out));
  Bit_Extender #(.in_width(5), .out_width(4)) bit_extender_3 (.in(Write_Register), .out(bit_extender_3_out));
  and and_1 (and_1_out, decoder_1_out0, RegWrite);
  and and_2 (and_2_out, decoder_1_out1, RegWrite);
  and and_3 (and_3_out, decoder_1_out2, RegWrite);
  and and_4 (and_4_out, decoder_1_out3, RegWrite);
  and and_5 (and_5_out, decoder_1_out4, RegWrite);
  and and_6 (and_6_out, decoder_1_out5, RegWrite);
  and and_7 (and_7_out, decoder_1_out6, RegWrite);
  and and_8 (and_8_out, decoder_1_out7, RegWrite);
  Clock clock (.out(clock_out));
  Register #(.width(16)) register_1 (.D(Write_Data), .en(and_1_out), .Q(register_1_q), .clk(clock_out));  // open: clr
  Register #(.width(16)) register_2 (.D(Write_Data), .en(and_2_out), .Q(register_2_q), .clk(clock_out));  // open: clr
  Register #(.width(16)) register_3 (.D(Write_Data), .en(and_3_out), .Q(register_3_q), .clk(clock_out));  // open: clr
  Register #(.width(16)) register_4 (.D(Write_Data), .en(and_4_out), .Q(register_4_q), .clk(clock_out));  // open: clr
  Register #(.width(16)) register_5 (.D(Write_Data), .en(and_5_out), .Q(register_5_q), .clk(clock_out));  // open: clr
  Register #(.width(16)) register_6 (.D(Write_Data), .en(and_6_out), .Q(register_6_q), .clk(clock_out));  // open: clr
  Register #(.width(16)) register_7 (.D(Write_Data), .en(and_7_out), .Q(register_7_q), .clk(clock_out));  // open: clr
  Register #(.width(16)) register_8 (.D(Write_Data), .en(and_8_out), .Q(register_8_q), .clk(clock_out));  // open: clr
  and and_9 (and_9_out, decoder_1_out8, RegWrite);
  and and_10 (and_10_out, decoder_1_out9, RegWrite);
  and and_11 (and_11_out, decoder_1_out10, RegWrite);
  and and_12 (and_12_out, decoder_1_out11, RegWrite);
  and and_13 (and_13_out, decoder_1_out12, RegWrite);
  and and_14 (and_14_out, decoder_1_out13, RegWrite);
  and and_15 (and_15_out, decoder_1_out14, RegWrite);
  and and_16 (and_16_out, decoder_1_out15, RegWrite);
  Register #(.width(16)) register_9 (.D(Write_Data), .en(and_9_out), .Q(register_9_q), .clk(clock_out));  // open: clr
  Register #(.width(16)) register_10 (
    .D(Write_Data), .en(and_10_out), .Q(register_10_q), .clk(clock_out));  // open: clr
  Register #(.width(16)) register_11 (
    .D(Write_Data), .en(and_11_out), .Q(register_11_q), .clk(clock_out));  // open: clr
  Register #(.width(16)) register_12 (
    .D(Write_Data), .en(and_12_out), .Q(register_12_q), .clk(clock_out));  // open: clr
  Register #(.width(16)) register_13 (
    .D(Write_Data), .en(and_13_out), .Q(register_13_q), .clk(clock_out));  // open: clr
  Register #(.width(16)) register_14 (
    .D(Write_Data), .en(and_14_out), .Q(register_14_q), .clk(clock_out));  // open: clr
  Register #(.width(16)) register_15 (
    .D(Write_Data), .en(and_15_out), .Q(register_15_q), .clk(clock_out));  // open: clr
  Register #(.width(16)) register_16 (
    .D(Write_Data), .en(and_16_out), .Q(register_16_q), .clk(clock_out));  // open: clr
  Multiplexer #(.select(4), .width(16)) multiplexer_1 (
    .in0(register_1_q), .in1(register_2_q), .in2(register_3_q), .in3(register_4_q), .in4(register_5_q),
    .in5(register_6_q), .in6(register_7_q), .in7(register_8_q), .in8(register_9_q), .in9(register_10_q),
    .in10(register_11_q), .in11(register_12_q), .in12(register_13_q), .in13(register_14_q),
    .in14(register_15_q), .in15(register_16_q), .out(Read_Data_1), .sel(bit_extender_1_out));  // open: en
  Multiplexer #(.select(4), .width(16)) multiplexer_2 (
    .in0(register_1_q), .in1(register_2_q), .in2(register_3_q), .in3(register_4_q), .in4(register_5_q),
    .in5(register_6_q), .in6(register_7_q), .in7(register_8_q), .in8(register_9_q), .in9(register_10_q),
    .in10(register_11_q), .in11(register_12_q), .in12(register_13_q), .in13(register_14_q),
    .in14(register_15_q), .in15(register_16_q), .out(Read_Data_2), .sel(bit_extender_2_out));  // open: en
endmodule

module ControlUnit (
  input  [5:0] Opcode,
  output Jump,
  output RegDst,
  output ALUSrc,
  output MemtoReg,
  output RegWrite,
  output MemRead,
  output MemWrite,
  output Branch,
  output [3:0] ALUop
);

  wire decoder_1_out0, decoder_1_out1, decoder_1_out2, decoder_1_out3, decoder_1_out4, decoder_1_out5,
       decoder_1_out6, decoder_1_out7, decoder_1_out8, decoder_1_out9, decoder_1_out10, decoder_1_out11,
       decoder_1_out12, decoder_1_out13, decoder_1_out14, decoder_1_out15;
  wire [3:0] bit_extender_1_out;

  Decoder #(.select(4)) decoder_1 (
    .out0(decoder_1_out0), .out1(decoder_1_out1), .out2(decoder_1_out2), .out3(decoder_1_out3),
    .out4(decoder_1_out4), .out5(decoder_1_out5), .out6(decoder_1_out6), .out7(decoder_1_out7),
    .out8(decoder_1_out8), .out9(decoder_1_out9), .out10(decoder_1_out10), .out11(decoder_1_out11),
    .out12(decoder_1_out12), .out13(decoder_1_out13), .out14(decoder_1_out14), .out15(decoder_1_out15),
    .sel(bit_extender_1_out));  // open: en
  Bit_Extender #(.in_width(6), .out_width(4)) bit_extender_1 (.in(Opcode), .out(bit_extender_1_out));
  MemWrite memwrite_1 (
    .\nor (decoder_1_out15), .add(decoder_1_out0), .sub(decoder_1_out1), .\and (decoder_1_out3),
    .\or (decoder_1_out4), .slt(decoder_1_out7), .load(decoder_1_out10), .addi(decoder_1_out5),
    .beq(decoder_1_out12), .blez(decoder_1_out13), .mult(decoder_1_out2), .mfhi(decoder_1_out8),
    .store(decoder_1_out11), .mflo(decoder_1_out9), .sll(decoder_1_out6), .MemWrite(MemWrite));
  RegDst regdst_1 (
    .\nor (decoder_1_out15), .add(decoder_1_out0), .sub(decoder_1_out1), .\and (decoder_1_out3),
    .\or (decoder_1_out4), .slt(decoder_1_out7), .sll(decoder_1_out6), .load(decoder_1_out10),
    .addi(decoder_1_out5), .RegDst(RegDst));
  Branch branch_1 (
    .\nor (decoder_1_out15), .add(decoder_1_out0), .sub(decoder_1_out1), .\and (decoder_1_out3),
    .\or (decoder_1_out4), .slt(decoder_1_out7), .load(decoder_1_out10), .store(decoder_1_out11),
    .addi(decoder_1_out5), .mult(decoder_1_out2), .mfhi(decoder_1_out8), .mflo(decoder_1_out9),
    .sll(decoder_1_out6), .beq(decoder_1_out12), .blez(decoder_1_out13), .Branch(Branch));
  ALUSrc alusrc_1 (
    .\nor (decoder_1_out15), .add(decoder_1_out0), .sub(decoder_1_out1), .\and (decoder_1_out3),
    .\or (decoder_1_out4), .slt(decoder_1_out7), .beq(decoder_1_out12), .mult(decoder_1_out2),
    .sll(decoder_1_out6), .load(decoder_1_out10), .store(decoder_1_out11), .addi(decoder_1_out5),
    .blez(decoder_1_out13), .ALUsrc(ALUSrc));
  Jump jump_1 (
    .add(decoder_1_out0), .sub(decoder_1_out1), .mult(decoder_1_out2), .\and (decoder_1_out3),
    .\or (decoder_1_out4), .addi(decoder_1_out5), .sll(decoder_1_out6), .slt(decoder_1_out7),
    .mfhi(decoder_1_out8), .mflo(decoder_1_out9), .load(decoder_1_out10), .store(decoder_1_out11),
    .beq(decoder_1_out12), .blez(decoder_1_out13), .J(decoder_1_out14), .\nor (decoder_1_out15), .Jump(Jump));
  MemtoReg memtoreg_1 (
    .add(decoder_1_out0), .sub(decoder_1_out1), .\and (decoder_1_out3), .\or (decoder_1_out4),
    .slt(decoder_1_out7), .addi(decoder_1_out5), .mfhi(decoder_1_out8), .mflo(decoder_1_out9),
    .load(decoder_1_out10), .sll(decoder_1_out6), .\nor (decoder_1_out15), .MemtoReg(MemtoReg));
  RegWrite regwrite_1 (
    .store(decoder_1_out11), .beq(decoder_1_out12), .blez(decoder_1_out13), .mult(decoder_1_out2),
    .sll(decoder_1_out6), .add(decoder_1_out0), .sub(decoder_1_out1), .\and (decoder_1_out3),
    .\or (decoder_1_out4), .slt(decoder_1_out7), .load(decoder_1_out10), .addi(decoder_1_out5),
    .mfhi(decoder_1_out8), .mflo(decoder_1_out9), .\nor (decoder_1_out15), .RegWrite(RegWrite));
  MemRead memread_1 (
    .\nor (decoder_1_out15), .add(decoder_1_out0), .sub(decoder_1_out1), .\and (decoder_1_out3),
    .\or (decoder_1_out4), .slt(decoder_1_out7), .store(decoder_1_out11), .addi(decoder_1_out5),
    .beq(decoder_1_out12), .blez(decoder_1_out13), .mult(decoder_1_out2), .mfhi(decoder_1_out8),
    .mflo(decoder_1_out9), .sll(decoder_1_out6), .load(decoder_1_out10), .MemRead(MemRead));
  ALUop aluop_1 (.OPCODE(bit_extender_1_out), .ALUop(ALUop));
endmodule

module RegDst (
  input  \nor ,
  input  add,
  input  sub,
  input  \and ,
  input  \or ,
  input  slt,
  input  sll,
  input  load,
  input  addi,
  output RegDst
);

  wire not_1_out, or_1_out, xor_1_out;

  or or_1 (or_1_out, load, addi);
  ExactlyOne xor_1 (.out(xor_1_out), .in0(add), .in1(sub), .in2(\and ), .in3(\nor ), .in4(\or ), .in5(slt), .in6(sll));
  not not_1 (not_1_out, or_1_out);
  and and_1 (RegDst, xor_1_out, not_1_out);
endmodule

module ALUSrc (
  input  \nor ,
  input  add,
  input  sub,
  input  \and ,
  input  \or ,
  input  slt,
  input  beq,
  input  mult,
  input  sll,
  input  load,
  input  store,
  input  addi,
  input  blez,
  output ALUsrc
);

  wire not_1_out, or_1_out, xor_1_out;

  ExactlyOne xor_1 (
    .out(xor_1_out), .in0(add), .in1(sub), .in2(\and ), .in3(\or ), .in4(\nor ), .in5(slt), .in6(beq),
    .in7(mult), .in8(sll));
  or or_1 (or_1_out, load, store, addi, blez);
  not not_1 (not_1_out, xor_1_out);
  and and_1 (ALUsrc, not_1_out, or_1_out);
endmodule

module MemtoReg (
  input  add,
  input  sub,
  input  \and ,
  input  \or ,
  input  slt,
  input  addi,
  input  mfhi,
  input  mflo,
  input  load,
  input  sll,
  input  \nor ,
  output MemtoReg
);

  wire not_1_out, xor_1_out;

  not not_1 (not_1_out, xor_1_out);
  ExactlyOne xor_1 (
    .out(xor_1_out), .in0(add), .in1(sub), .in2(\and ), .in3(\or ), .in4(slt), .in5(addi), .in6(mfhi),
    .in7(mflo), .in8(sll), .in9(\nor ));
  and and_1 (MemtoReg, not_1_out, load);
endmodule

module RegWrite (
  input  store,
  input  beq,
  input  blez,
  input  mult,
  input  sll,
  input  add,
  input  sub,
  input  \and ,
  input  \or ,
  input  slt,
  input  load,
  input  addi,
  input  mfhi,
  input  mflo,
  input  \nor ,
  output RegWrite
);

  wire nor_1_out, or_1_out;

  or or_1 (or_1_out, add, sub, \and , \or , slt, load, addi, mfhi, mflo, \nor );
  nor nor_1 (nor_1_out, store, beq, blez, mult, sll);
  and and_1 (RegWrite, nor_1_out, or_1_out);
endmodule

module MemRead (
  input  \nor ,
  input  add,
  input  sub,
  input  \and ,
  input  \or ,
  input  slt,
  input  store,
  input  addi,
  input  beq,
  input  blez,
  input  mult,
  input  mfhi,
  input  mflo,
  input  sll,
  input  load,
  output MemRead
);

  wire nor_1_out;

  nor nor_1 (nor_1_out, \nor , add, sub, \and , \or , slt, store, addi, beq, blez, mult, mfhi, mflo, sll);
  and and_1 (MemRead, nor_1_out, load);
endmodule

module MemWrite (
  input  \nor ,
  input  add,
  input  sub,
  input  \and ,
  input  \or ,
  input  slt,
  input  load,
  input  addi,
  input  beq,
  input  blez,
  input  mult,
  input  mfhi,
  input  store,
  input  mflo,
  input  sll,
  output MemWrite
);

  wire nor_1_out;

  nor nor_1 (nor_1_out, \nor , add, sub, \and , \or , slt, load, addi, beq, blez, mult, mfhi, mflo, sll);
  and and_1 (MemWrite, nor_1_out, store);
endmodule

module Branch (
  input  \nor ,
  input  add,
  input  sub,
  input  \and ,
  input  \or ,
  input  slt,
  input  load,
  input  store,
  input  addi,
  input  mult,
  input  mfhi,
  input  mflo,
  input  sll,
  input  beq,
  input  blez,
  output Branch
);

  wire nor_1_out, or_1_out;

  nor nor_1 (nor_1_out, add, sub, \and , \or , slt, load, \nor , store, addi, mult, mfhi, mflo, sll);
  or or_1 (or_1_out, beq, blez);
  and and_1 (Branch, nor_1_out, or_1_out);
endmodule

module Splitter (
  input  [31:0] in_1,
  output [5:0] Opcode,
  output [4:0] rs,
  output [4:0] rt,
  output [4:0] rd,
  output [4:0] shamt,
  output [15:0] _0_15
);


  assign _0_15 = in_1[15:0];
  assign Opcode = in_1[31:26];
  assign rd = in_1[15:11];
  assign rs = in_1[25:21];
  assign rt = in_1[20:16];
  assign shamt = in_1[10:6];
endmodule

module Jump (
  input  add,
  input  sub,
  input  mult,
  input  \and ,
  input  \or ,
  input  addi,
  input  sll,
  input  slt,
  input  mfhi,
  input  mflo,
  input  load,
  input  store,
  input  beq,
  input  blez,
  input  J,
  input  \nor ,
  output Jump
);

  wire nor_1_out;

  nor nor_1 (nor_1_out, add, sub, mult, \and , \or , addi, sll, \nor , slt, mfhi, mflo, load, store, beq, blez);
  and and_1 (Jump, J, nor_1_out);
endmodule

module ALUop (
  input  [3:0] OPCODE,
  output [3:0] ALUop
);

  Multiplexer #(.select(4), .width(4)) multiplexer_1 (
    .in0(4'b0000), .in1(4'b0001), .in2(4'b0010), .in3(4'b0011), .in4(4'b0100), .in5(4'b0000), .in6(4'b0110),
    .in7(4'b0111), .in8(4'b1000), .in9(4'b1001), .in10(4'b0000), .in11(4'b0000), .in12(4'b0001),
    .in13(4'b0001), .in15(OPCODE), .out(ALUop), .sel(OPCODE));  // open: in14, en
endmodule
